# Fritzing sketch rf24-softSPI_plusEthernetShield (saved by Fritzing 0.8.5b)

parts:
  Part1 = Arduino Ethernet Shield (Rev3)
  NRF24L1 = NRF24L01

nets:
  N1: Part1.A0, NRF24L1.SCK
  N2: Part1.A1, NRF24L1.MOSI
  N3: Part1.A2, NRF24L1.MISO
  N4: Part1.PWM_D6, NRF24L1.CE
  N5: Part1.D7, NRF24L1.CSN
  3V3: Part1.3V3, NRF24L1.VCC
  GND: Part1.GND, NRF24L1.GND

custom parts:
  NRF24L01: NRF24L01 module
